# Fritzing sketch led_pots_one_colour (saved by Fritzing 0.9.2b)
breadboards: 1

parts:
  VCC1 = Battery block 9V
  R1 = Resistor [tolerance=±5% resistance=220 package=THT]
  R4 = Rotary Potentiometer (Small) [maximum_resistance=100kΩ package=THT]
  LED1 = LED - 5mm [color="Red (633nm)" package="5 mm [THT]"]  # not connected

nets:
  N1: VCC1.-, R1.Pin_0, R4.leg1
  N2: VCC1.+, R4.leg2

notes:
  Be SUPER careful with the pot. Only connect the power to the two OUTSIDE pins, as shown.
  If you connect to pins 1+2 or 2+3, you could make the pot get hot, melt, and make a nasty smell. The battery could also get hot.
