# Fritzing sketch led_pots_threecolours (saved by Fritzing 0.9.2b)
breadboards: 1

parts:
  VCC1 = Battery block 9V
  LED1 = RGB LED (com. cathode, rgb) [package="5 mm [THT]"]
  R2 = Rotary Potentiometer (Small) [maximum_resistance=100kΩ package=THT]
  R3 = Rotary Potentiometer (Small) [maximum_resistance=100kΩ package=THT]
  R4 = Rotary Potentiometer (Small) [maximum_resistance=100kΩ package=THT]
  R5 = Resistor [tolerance=±5% resistance=220 package=THT]
  R6 = Resistor [tolerance=±5% resistance=220 package=THT]
  R7 = Resistor [tolerance=±5% resistance=220 package=THT]

nets:
  N1: VCC1.-, LED1.common_cathode, R2.leg1, R3.leg1, R4.leg1
  N2: VCC1.+, R2.leg2, R3.leg2, R4.leg2
  N3: LED1.red_anode, R6.Pin_1
  N4: LED1.green_anode, R7.Pin_1
  N5: LED1.blue_anode, R5.Pin_1
  N6: R2.wiper, R5.Pin_0
  N7: R3.wiper, R7.Pin_0
  N8: R4.wiper, R6.Pin_0

notes:
  DON'T FORGET THE PING PONG BALL!
  This version will work better than the one we did in class, because it has one resistor for each LED.
