# Fritzing sketch led_switch (saved by Fritzing 0.9.2b)
breadboards: 1

parts:
  VCC1 = Battery block 9V
  R1 = Resistor [tolerance=±5% resistance=220 package=THT]
  LED1 = LED - 5mm [color="Red (633nm)" package="5 mm [THT]"]
  S2 = Pushbutton [package=THT]

nets:
  N1: VCC1.-, R1.Pin_1
  N2: VCC1.+, S2.leg0
  N3: R1.Pin_0, LED1.cathode
  N4: LED1.anode, S2.leg1
