# Fritzing sketch led_switch_three_LEDs (saved by Fritzing 0.9.2b)
breadboards: 1

parts:
  VCC1 = Battery block 9V
  R1 = Resistor [tolerance=±5% resistance=220 package=THT]
  S1 = Pushbutton [package=THT]
  S2 = Pushbutton [package=THT]
  S3 = Pushbutton [package=THT]
  LED1 = LED - 5mm [color="Red (633nm)" package="5 mm [THT]"]
  LED2 = LED - 5mm [color="Green (565nm)" package="5 mm [THT]"]
  LED3 = LED - 5mm [color="Yellow (595nm)" package="5 mm [THT]"]
  R2 = Resistor [tolerance=±5% resistance=220 package=THT]
  R3 = Resistor [tolerance=±5% resistance=220 package=THT]

nets:
  N1: VCC1.-, R1.Pin_0, S2.leg0, LED1.cathode, LED2.cathode, LED3.cathode
  N2: VCC1.+, S1.leg1, S2.leg1, S3.leg1
  N3: R1.Pin_1, LED2.anode
  N4: S1.leg0, R3.Pin_0
  N5: S3.leg0, R2.Pin_0
  N6: LED1.anode, R2.Pin_1
  N7: LED3.anode, R3.Pin_1

notes:
  Remember, with single LEDs, the LONG leg goes to + (the red wire)
  If your LEDs don't light, follow the path of the red wire - it should go into one side of the switch, out the other side, through the resistor and into the LED.
  This arrangement is done properly, with 3 resistors. You should be able to mix colours by pressing two buttons at once
