# Fritzing sketch led_switch_threecolours (saved by Fritzing 0.9.2b)
breadboards: 1

parts:
  VCC1 = Battery block 9V
  LED1 = RGB LED (com. cathode, rgb) [package="5 mm [THT]"]
  S1 = Pushbutton [package=THT]
  S2 = Pushbutton [package=THT]
  S3 = Pushbutton [package=THT]
  R1 = Resistor [tolerance=±5% resistance=220 package=THT]
  R2 = Resistor [tolerance=±5% resistance=220 package=THT]
  R3 = Resistor [tolerance=±5% resistance=220 package=THT]

nets:
  N1: VCC1.-, LED1.common_cathode
  N2: VCC1.+, S1.leg1, S2.leg1, S3.leg1
  N3: LED1.red_anode, R1.Pin_1
  N4: LED1.green_anode, R2.Pin_1
  N5: LED1.blue_anode, R3.Pin_1
  N6: S1.leg0, R3.Pin_0
  N7: S2.leg0, R2.Pin_0
  N8: S3.leg0, R1.Pin_0

notes:
  The LONG pin in the coloured LED goes to black/blue/negative
  Put one resistor on the LONG pin, and the LED will be protected.
  Get ONE switch working first - plug it into each of the 3 pins to check all the colours work, then start to connect the other switches
