# Fritzing sketch oscillator (saved by Fritzing 0.9.2b)
breadboards: 1

parts:
  VCC1 = Battery block 9V
  R4 = Rotary Potentiometer (Small) [maximum_resistance=100kΩ package=THT]
  IC2 = IC, DIP package, 14 pins [chip_label=40106 spacing=300mil]
  C1 = Capacitor [package=cap-pth-small2]
  SP1 = SPEAKER [package=pcb_mount_speaker]
  C2 = Electrolytic Capacitor [capacitance=1µF package="100 mil [THT, electrolytic]"]

nets:
  N1: VCC1.-, IC2.pin7, C1.1, SP1.+
  N2: VCC1.+, IC2.pin14
  N3: R4.wiper, IC2.pin12, C2.+
  N4: R4.leg2, IC2.pin13, C1.2
  N5: SP1.-, C2.-

notes:
  NB, the hole on the chip is at THIS END
  Bend the chip legs gently to fit them into the breadboard
