# Fritzing sketch led_no_switch (saved by Fritzing 0.9.2b)
breadboards: 1

parts:
  VCC1 = Battery block 9V
  R1 = Resistor [tolerance=±5% resistance=220 package=THT]
  LED1 = LED - 5mm [color="Red (633nm)" package="5 mm [THT]"]

nets:
  N1: VCC1.-, R1.Pin_1
  N2: VCC1.+, LED1.anode
  N3: R1.Pin_0, LED1.cathode

notes:
  How to get your LED the right way around:
  The LONG leg goes to RED/Positive
  The SHORT leg also has a flat side on the plastic bit
