# Fritzing sketch led_pots_threecolours (saved by Fritzing 0.9.2b)
breadboards: 1

parts:
  VCC1 = Battery block 9V
  LED1 = RGB LED (com. cathode, rgb) [package="5 mm [THT]"]
  R1 = Resistor [tolerance=±5% resistance=220 package=THT]
  R2 = Rotary Potentiometer (Small) [maximum_resistance=100kΩ package=THT]
  R3 = Rotary Potentiometer (Small) [maximum_resistance=100kΩ package=THT]
  R4 = Rotary Potentiometer (Small) [maximum_resistance=100kΩ package=THT]

nets:
  N1: VCC1.-, R1.Pin_0, R2.leg1, R3.leg1, R4.leg1
  N2: VCC1.+, R2.leg2, R3.leg2, R4.leg2
  N3: LED1.red_anode, R2.wiper
  N4: LED1.common_cathode, R1.Pin_1
  N5: LED1.green_anode, R3.wiper
  N6: LED1.blue_anode, R4.wiper
