# Fritzing sketch led_switch_three_LEDs (saved by Fritzing 0.9.2b)
breadboards: 1

parts:
  VCC1 = Battery block 9V
  R1 = Resistor [tolerance=±5% resistance=220 package=THT]
  S1 = Pushbutton [package=THT]
  S2 = Pushbutton [package=THT]
  S3 = Pushbutton [package=THT]
  LED1 = LED - 5mm [color="Red (633nm)" package="5 mm [THT]"]
  LED2 = LED - 5mm [color="Green (565nm)" package="5 mm [THT]"]
  LED3 = LED - 5mm [color="Yellow (595nm)" package="5 mm [THT]"]

nets:
  N1: VCC1.-, R1.Pin_0
  N2: VCC1.+, S1.leg1, S2.leg1, S3.leg1
  N3: R1.Pin_1, LED1.cathode, LED2.cathode, LED3.cathode
  N4: S1.leg0, LED3.anode
  N5: S2.leg0, LED2.anode
  N6: S3.leg0, LED1.anode

notes:
  You should really use three resistors, one for each LED, but this will work. See if you can spot the brightness of one LED changing when you turn on others.
  Get ONE switch working first, then start to connect the other switches
